# Fritzing sketch botonInicioPausa (saved by Fritzing 0.9.3b)
breadboards: 2

parts:
  Mod1 = Raspberry Pi Pico W
  7_Segment1 = 7 Segment Display
  R1 = Resistor [tolerance=±5% resistance=220 package="0805 [SMD]"]
  S1 = Momentary Switch [package=ksa_sealed_tac_switch]

nets:
  N1: Mod1.pin_1, S1.2
  N2: Mod1.pin_3, Mod1.pin_8, Mod1.pin_13, Mod1.pin_18, Mod1.pin_23, Mod1.pin_28, Mod1.pin_33, Mod1.pin_38, R1.Pin_1, S1.3
  N3: Mod1.pin_4, 7_Segment1.Segment_A
  N4: Mod1.pin_5, 7_Segment1.Segment_B
  N5: Mod1.pin_6, 7_Segment1.Segment_C
  N6: Mod1.pin_7, 7_Segment1.Segment_D
  N7: Mod1.pin_9, 7_Segment1.Segment_E
  N8: Mod1.pin_10, 7_Segment1.Segment_F
  N9: Mod1.pin_11, 7_Segment1.Segment_G
  N10: 7_Segment1.common_cathode, R1.Pin_0

custom parts:
  Raspberry Pi Pico W: Raspberry Pi Pico W. Based around the RP2040 microcontroller the Pico W is a low cost microcontroller device bringing Raspberry Pi quality, cost, and easy of use to the microcontroller space. The areas marked KEEPOUT in pcb silkscreen should not have traces running through them to avoid shorts on a soldered in module!
